// Logisim project OCLE - Práctica 1 (parte I).circ as structural Verilog: 1 circuit, main circuit main
module main (
  input  [10:0] in_1,
  input  CS,
  input  Clear,
  input  [23:0] Escritura,
  input  W_prime___R,
  output [23:0] Lectura
);

  wire not_1_out;
  wire [23:0] ram_1_data;

  RAM #(.addrWidth(11), .dataWidth(24), .bus("asynch")) ram_1 (
    .addr(in_1), .data(ram_1_data), .sel(CS), .ld(W_prime___R), .clr(Clear));
  assign Lectura = W_prime___R ? ram_1_data : 24'bz;  // Controlled_Buffer controlled_buffer_1
  assign ram_1_data = not_1_out ? Escritura : 24'bz;  // Controlled_Buffer controlled_buffer_2
  not not_1 (not_1_out, W_prime___R);

  // Notes on the sheet:
  //   Bus de direcciones
  //   Buses de control
  //   Diseñe y simule en logisim una memoria RAM asícrona de tamaño 2048 x 24 bits
  //   Memoria RAM
  //   Bus de datos
  //   2^11 = 2048
endmodule
