// Logisim project OCLE - Práctica 1 (parte II).circ as structural Verilog: 1 circuit, main circuit main
module main (
  input  [10:0] Bus_de_direcciones,
  input  W_prime___R,
  input  Clear,
  input  Enable,
  input  [23:0] Escritura,
  output [23:0] Lectura
);

  wire and_1_out, and_2_out, not_1_out, not_2_out;
  wire [23:0] controlled_buffer_2_out;

  and and_1 (and_1_out, Bus_de_direcciones[10], Enable);
  not not_1 (not_1_out, Bus_de_direcciones[10]);
  and and_2 (and_2_out, not_1_out, Enable);
  assign Lectura = W_prime___R ? controlled_buffer_2_out : 24'bz;  // Controlled_Buffer controlled_buffer_1
  not not_2 (not_2_out, W_prime___R);
  assign controlled_buffer_2_out = not_2_out ? Escritura : 24'bz;  // Controlled_Buffer controlled_buffer_2
  RAM #(.addrWidth(10), .bus("asynch")) ram_1 (
    .addr(Bus_de_direcciones[9:0]), .data(controlled_buffer_2_out[7:0]), .sel(and_1_out), .ld(W_prime___R),
    .clr(Clear));
  RAM #(.addrWidth(10), .bus("asynch")) ram_2 (
    .addr(Bus_de_direcciones[9:0]), .data(controlled_buffer_2_out[7:0]), .sel(and_2_out), .ld(W_prime___R),
    .clr(Clear));
  RAM #(.addrWidth(10), .bus("asynch")) ram_3 (
    .addr(Bus_de_direcciones[9:0]), .data(controlled_buffer_2_out[15:8]), .sel(and_1_out), .ld(W_prime___R),
    .clr(Clear));
  RAM #(.addrWidth(10), .bus("asynch")) ram_4 (
    .addr(Bus_de_direcciones[9:0]), .data(controlled_buffer_2_out[15:8]), .sel(and_2_out), .ld(W_prime___R),
    .clr(Clear));
  RAM #(.addrWidth(10), .bus("asynch")) ram_5 (
    .addr(Bus_de_direcciones[9:0]), .data(controlled_buffer_2_out[23:16]), .sel(and_1_out), .ld(W_prime___R),
    .clr(Clear));
  RAM #(.addrWidth(10), .bus("asynch")) ram_6 (
    .addr(Bus_de_direcciones[9:0]), .data(controlled_buffer_2_out[23:16]), .sel(and_2_out), .ld(W_prime___R),
    .clr(Clear));
endmodule
