// Logisim project OCLE - Práctica 2 (parte A I).circ as structural Verilog: 1 circuit, main circuit main
module main (
  input  [23:0] in_1,
  input  in_2,
  input  [23:0] in_3,
  output [23:0] out_4
);

  wire and_1_out, not_1_out, not_2_out, not_3_out, not_4_out, not_5_out, not_6_out, not_7_out, not_8_out,
       not_9_out, not_10_out, or_1_out;

  not not_1 (not_1_out, in_3[0]);
  not not_2 (not_2_out, in_3[2]);
  not not_3 (not_3_out, in_3[3]);
  not not_4 (not_4_out, in_3[6]);
  not not_5 (not_5_out, in_3[10]);
  not not_6 (not_6_out, in_3[13]);
  not not_7 (not_7_out, in_3[15]);
  not not_8 (not_8_out, in_3[11]);
  not not_9 (not_9_out, in_3[14]);
  or or_1 (or_1_out, not_1_out, in_3[1], not_2_out, not_3_out, in_3[4], in_3[5], not_4_out, in_3[7], in_3[8], in_3[9], not_5_out, not_8_out, in_3[12], not_6_out, not_9_out, not_7_out, in_3[16], in_3[17], in_3[18], in_3[19], in_3[20], in_3[21], in_3[22], in_3[23]);
  Register #(.width(24), .trigger("low")) register_1 (.D(in_1), .Q(out_4), .clk(not_10_out));  // open: en, clr
  not not_10 (not_10_out, and_1_out);
  and and_1 (and_1_out, ~in_2, ~or_1_out);  // AND_Gate

  // Notes on the sheet:
  //   Consideraciones
  //   1.  Primero se ajusta la dirección
  //   2. Después se coloca los datos
  //   BUS de direcciones
  //   3. Finalmente madará la señal de control de escritura
  //   INSTRUCCIONES: Simular un puerto de salida de 24 bits que responde a la dirección EC4Dh
  //   Decodificador de direccion para EC4Dh
  //   Decodificador empelando puerta OR (teorema de De-Morgan)
  //   BUS DE DATOS
  //   EC4Dh = 1110 1100 0100 1101
  //   ______
  //   IOWR
  //   Un latch es un elemento de memoria que se activa por nivel,
  //   en este caso se usa un registro (configurado para que se active por nivel)
  //   LATCH
  //   se activa en baja
  //   SALIDA
endmodule
