// Logisim project OCLE - Práctica 2 (parte A II).circ as structural Verilog: 1 circuit, main circuit main
module main (
  input  [23:0] in_1,
  input  in_2,
  input  [23:0] in_3,
  output [23:0] out_4
);

  wire and_1_out, not_1_out, not_2_out, not_3_out, not_4_out, not_5_out, not_6_out, not_7_out, not_8_out,
       not_9_out, or_1_out;

  not not_1 (not_1_out, in_3[1]);
  not not_2 (not_2_out, in_3[3]);
  not not_3 (not_3_out, in_3[6]);
  not not_4 (not_4_out, in_3[10]);
  not not_5 (not_5_out, in_3[13]);
  not not_6 (not_6_out, in_3[15]);
  not not_7 (not_7_out, in_3[2]);
  not not_8 (not_8_out, in_3[11]);
  not not_9 (not_9_out, in_3[14]);
  or or_1 (or_1_out, in_3[0], not_1_out, not_7_out, not_2_out, in_3[4], in_3[5], not_3_out, in_3[7], in_3[8], in_3[9], not_4_out, not_8_out, in_3[12], not_5_out, not_9_out, not_6_out, in_3[16], in_3[17], in_3[18], in_3[19], in_3[20], in_3[21], in_3[22], in_3[23]);
  assign out_4 = and_1_out ? in_1 : 24'bz;  // Controlled_Buffer controlled_buffer_1
  and and_1 (and_1_out, ~in_2, ~or_1_out);  // AND_Gate

  // Notes on the sheet:
  //   Consideraciones
  //   1.  Primero se ajusta la dirección
  //   2. Después se manda la señal
  //   3. Finalmente se lee el dato
  //   BUS de direcciones
  //   INSTRUCCIONES: Simular un puerto de entrada de 24 bits que responde a la dirección EC4Eh
  //   Decodificador de direccion para EC4Dh
  //   Decodificador empelando puerta OR (teorema de De-Morgan)
  //   EC4Eh = 1110 1100 0100 1110
  //   BUS DE DATOS
  //   ______
  //   IORD
  //   Buffer tri-state
  //   ENTRADA
endmodule
