// Logisim project OCLE - Práctica 2 (parte B).circ as structural Verilog: 2 circuits, main circuit main
module main (
  input  [3:0] in_1,
  input  in_2,
  input  [9:0] in_3,
  input  in_4,
  input  in_5,
  input  [3:0] in_6,
  output [7:0] out_7,
  output [7:0] out_8,
  output [7:0] out_9
);

  wire clock_1_out, demultiplexer_3_out0, demultiplexer_3_out1, demultiplexer_3_out2, demultiplexer_3_out3,
       not_1_out, not_2_out;
  wire [3:0] controlled_buffer_3_out, controlled_buffer_4_out, demultiplexer_2_out0, demultiplexer_2_out1,
       demultiplexer_2_out2, demultiplexer_2_out3, multiplexer_1_out, register_1_q, register_2_q,
       register_3_q, register_4_q;
  wire [7:0] demultiplexer_1_out3;
  wire [9:0] controlled_buffer_1_out, ram_1_data;

  Demultiplexer #(.select(2), .width(8), .enable("false")) demultiplexer_1 (
    .out0(out_7), .out1(out_8), .out2(out_9), .out3(demultiplexer_1_out3), .in(controlled_buffer_1_out[7:0]),
    .sel(controlled_buffer_1_out[9:8]));
  RAM #(.addrWidth(4), .dataWidth(10), .bus("asynch")) ram_1 (
    .addr(in_1), .data(ram_1_data), .sel(in_4), .ld(in_5), .clr(in_2));
  not not_1 (not_1_out, in_5);
  Demultiplexer #(.select(2), .width(4), .disabled(0), .enable("false")) demultiplexer_2 (
    .out0(demultiplexer_2_out0), .out1(demultiplexer_2_out1), .out2(demultiplexer_2_out2),
    .out3(demultiplexer_2_out3), .in(controlled_buffer_3_out), .sel(demultiplexer_1_out3[1:0]));
  Demultiplexer #(.select(2), .enable("false")) demultiplexer_3 (
    .out0(demultiplexer_3_out0), .out1(demultiplexer_3_out1), .out2(demultiplexer_3_out2),
    .out3(demultiplexer_3_out3), .in(1'b1), .sel(demultiplexer_1_out3[1:0]));
  assign controlled_buffer_1_out = in_5 ? ram_1_data : 10'bz;  // Controlled_Buffer controlled_buffer_1
  assign ram_1_data = not_1_out ? in_3 : 10'bz;  // Controlled_Buffer controlled_buffer_2
  Clock clock_1 (.out(clock_1_out));
  Register #(.width(4)) register_1 (
    .D(demultiplexer_2_out0), .en(demultiplexer_3_out0), .Q(register_1_q), .clk(clock_1_out));  // open: clr
  Register #(.width(4)) register_2 (
    .D(demultiplexer_2_out1), .en(demultiplexer_3_out1), .Q(register_2_q), .clk(clock_1_out));  // open: clr
  Register #(.width(4)) register_3 (
    .D(demultiplexer_2_out2), .en(demultiplexer_3_out2), .Q(register_3_q), .clk(clock_1_out));  // open: clr
  Register #(.width(4)) register_4 (
    .D(demultiplexer_2_out3), .en(demultiplexer_3_out3), .Q(register_4_q), .clk(clock_1_out));  // open: clr
  assign controlled_buffer_3_out = demultiplexer_1_out3[3] ? in_6 : 4'bz;  // Controlled_Buffer controlled_buffer_3
  Multiplexer #(.select(2), .width(4), .enable("false")) multiplexer_1 (
    .in0(register_1_q), .in1(register_2_q), .in2(register_3_q), .in3(register_4_q), .out(multiplexer_1_out),
    .sel(demultiplexer_1_out3[1:0]));
  assign controlled_buffer_4_out = not_2_out ? multiplexer_1_out : 4'bz;  // Controlled_Buffer controlled_buffer_4
  Hex_Digit_Display hex_digit_display_1 (.value(controlled_buffer_4_out));  // open: dp
  not not_2 (not_2_out, demultiplexer_1_out3[3]);

  // Notes on the sheet:
  //   Código de operación de E/S: 11 00 00 L H RN
  //   RN = Número de registro (en pdf aparece como D)
endmodule

module E_S (
  input  [1:0] R0_R3,
  input  [3:0] Lectura,
  output [3:0] Escritura
);

  wire clock_1_out, demultiplexer_2_out0, demultiplexer_2_out1, demultiplexer_2_out2, demultiplexer_2_out3;
  wire [3:0] demultiplexer_1_out0, demultiplexer_1_out1, demultiplexer_1_out2, demultiplexer_1_out3,
       register_1_q, register_2_q, register_3_q, register_4_q;

  Demultiplexer #(.select(2), .width(4), .disabled(0), .enable("false")) demultiplexer_1 (
    .out0(demultiplexer_1_out0), .out1(demultiplexer_1_out1), .out2(demultiplexer_1_out2),
    .out3(demultiplexer_1_out3), .in(Lectura), .sel(R0_R3));
  Demultiplexer #(.select(2), .enable("false")) demultiplexer_2 (
    .out0(demultiplexer_2_out0), .out1(demultiplexer_2_out1), .out2(demultiplexer_2_out2),
    .out3(demultiplexer_2_out3), .in(1'b1), .sel(R0_R3));
  Clock clock_1 (.out(clock_1_out));
  Register #(.width(4)) register_1 (
    .D(demultiplexer_1_out0), .en(demultiplexer_2_out0), .Q(register_1_q), .clk(clock_1_out));  // open: clr
  Register #(.width(4)) register_2 (
    .D(demultiplexer_1_out1), .en(demultiplexer_2_out1), .Q(register_2_q), .clk(clock_1_out));  // open: clr
  Register #(.width(4)) register_3 (
    .D(demultiplexer_1_out2), .en(demultiplexer_2_out2), .Q(register_3_q), .clk(clock_1_out));  // open: clr
  Register #(.width(4)) register_4 (
    .D(demultiplexer_1_out3), .en(demultiplexer_2_out3), .Q(register_4_q), .clk(clock_1_out));  // open: clr
  Multiplexer #(.select(2), .width(4), .enable("false")) multiplexer_1 (
    .in0(register_1_q), .in1(register_2_q), .in2(register_3_q), .in3(register_4_q), .out(Escritura));  // open: sel
endmodule
